// Logisim project TP10.circ as structural Verilog: 10 circuits, main circuit Ejercicio 2
module Sum_1 (
  input  A,
  input  B,
  input  Cin,
  output Salida,
  output Carry_Out
);

  wire and_1_out, and_2_out, xor_1_out;

  xor xor_1 (xor_1_out, A, B);
  and and_1 (and_1_out, A, B);
  and and_2 (and_2_out, xor_1_out, Cin);
  xor xor_2 (Salida, xor_1_out, Cin);
  xor xor_3 (Carry_Out, and_2_out, and_1_out);
endmodule

module Ejercicio_2 (
  input  C,
  input  B,
  input  A,
  output out_4
);

  wire and_1_out, and_2_out, and_3_out, and_4_out, and_5_out, not_1_out, not_2_out, not_3_out;

  not not_1 (not_1_out, C);
  not not_2 (not_2_out, B);
  not not_3 (not_3_out, A);
  and and_1 (and_1_out, not_3_out, not_2_out, not_1_out);
  and and_2 (and_2_out, not_3_out, B, C);
  and and_3 (and_3_out, not_3_out, B, not_1_out);
  and and_4 (and_4_out, A, not_2_out, not_1_out);
  and and_5 (and_5_out, A, B, not_1_out);
  or or_1 (out_4, and_1_out, and_2_out, and_3_out, and_4_out, and_5_out);

  // Notes on the sheet:
  //   S = A'B'C' + A'BC + A'BC' + AB'C' + ABC'  
endmodule

module UC (
  input  C2,
  input  C1,
  input  C0,
  output AR,
  output I_prime,
  output CS,
  output R_W_prime,
  output AR__NAND,
  output I_prime__NOR
);

  wire nand_1_out, nor_1_out, nor_2_out, not_1_out, not_2_out, or_1_out, or_2_out;

  not not_1 (not_1_out, C2);
  not not_2 (not_2_out, C1);
  not not_3 (CS, C0);
  and and_1 (AR, C0, C1, not_1_out);
  or or_1 (or_1_out, not_1_out, CS);
  or or_2 (or_2_out, not_1_out, C1);
  or or_3 (R_W_prime, C2, not_2_out, CS);
  not nand_1 (nand_1_out, C1);  // NAND_Gate
  nor nor_1 (nor_1_out, not_1_out, CS);
  nor nor_2 (nor_2_out, not_1_out, C1);
  and and_2 (I_prime, or_1_out, or_2_out);
  nand nand_2 (AR__NAND, nand_1_out, nand_1_out);
  nor nor_3 (I_prime__NOR, nor_1_out, nor_2_out);
endmodule

module Sum_8 (
  input  [7:0] in_1,
  input  [7:0] in_2,
  input  [7:0] in_3,
  output Co
);

  wire sum_1_1_salida, sum_1_2_salida, sum_1_3_salida, sum_1_4_salida, sum_1_5_salida, sum_1_6_salida,
       sum_1_7_salida, sum_1_8_salida;

  Sum_1 sum_1_1 (.A(in_1[0]), .B(in_3[0]), .Cin(sum_1_2_salida), .Salida(sum_1_1_salida), .Carry_Out(in_2[0]));
  Sum_1 sum_1_2 (.A(in_1[1]), .B(in_3[1]), .Cin(sum_1_3_salida), .Salida(sum_1_2_salida), .Carry_Out(in_2[1]));
  Sum_1 sum_1_3 (.A(in_1[2]), .B(in_3[2]), .Cin(sum_1_4_salida), .Salida(sum_1_3_salida), .Carry_Out(in_2[2]));
  Sum_1 sum_1_4 (.A(in_1[3]), .B(in_3[3]), .Cin(sum_1_5_salida), .Salida(sum_1_4_salida), .Carry_Out(in_2[3]));
  Sum_1 sum_1_5 (.A(in_1[4]), .B(in_3[4]), .Cin(sum_1_6_salida), .Salida(sum_1_5_salida), .Carry_Out(in_2[4]));
  Sum_1 sum_1_6 (.A(in_1[5]), .B(in_3[5]), .Cin(sum_1_7_salida), .Salida(sum_1_6_salida), .Carry_Out(in_2[5]));
  Sum_1 sum_1_7 (.A(in_1[6]), .B(in_3[6]), .Cin(sum_1_8_salida), .Salida(sum_1_7_salida), .Carry_Out(in_2[6]));
  Sum_1 sum_1_8 (.A(in_1[7]), .B(in_3[7]), .Cin(Co), .Salida(sum_1_8_salida), .Carry_Out(in_2[7]));
  // also tied to GND on the sheet: sum_1_1_salida
endmodule

module Sum_32 (
  input  [31:0] T,
  input  [31:0] U,
  output [31:0] Z,
  output C
);

  Adder #(.width(32)) adder_1 (.a(T), .b(U), .out(Z), .cin(1'b0), .cout(C));

  // Notes on the sheet:
  //   U: pull=up
endmodule

module Deco_2a4 (
  input  S1,
  input  S0,
  output D0,
  output D1,
  output D2,
  output D3
);

  wire not_1_out, not_2_out;

  and and_1 (D0, not_1_out, not_2_out);
  not not_1 (not_1_out, S1);
  not not_2 (not_2_out, S0);
  and and_2 (D1, not_1_out, S0);
  and and_3 (D2, S1, not_2_out);
  and and_4 (D3, S1, S0);
endmodule

module Deco_8 (
  input  S2,
  input  S1,
  input  S0,
  output D0,
  output D1,
  output D2,
  output D3,
  output D4,
  output D5,
  output D6,
  output D7
);

  wire not_1_out, not_2_out, not_3_out;

  and and_1 (D0, not_1_out, not_2_out, not_3_out);
  not not_1 (not_1_out, S2);
  not not_2 (not_2_out, S1);
  not not_3 (not_3_out, S0);
  and and_2 (D1, not_1_out, not_2_out, S0);
  and and_3 (D2, not_1_out, S1, not_3_out);
  and and_4 (D3, not_1_out, S1, S0);
  and and_5 (D4, S2, not_2_out, not_3_out);
  and and_6 (D5, S2, not_2_out, S0);
  and and_7 (D6, S2, S1, not_3_out);
  and and_8 (D7, S2, S1, S0);
endmodule

module Mux_4 (
  input  I0,
  input  I1,
  input  I2,
  input  I3,
  input  S1,
  input  S0,
  output O
);

  wire and_1_out, and_2_out, and_3_out, and_4_out, deco_2a4_1_d0, deco_2a4_1_d1, deco_2a4_1_d2, deco_2a4_1_d3;

  Deco_2a4 deco_2a4_1 (
    .S1(S1), .S0(S0), .D0(deco_2a4_1_d0), .D1(deco_2a4_1_d1), .D2(deco_2a4_1_d2), .D3(deco_2a4_1_d3));
  and and_1 (and_1_out, I0, deco_2a4_1_d0);
  and and_2 (and_2_out, I1, deco_2a4_1_d1);
  and and_3 (and_3_out, I2, deco_2a4_1_d2);
  and and_4 (and_4_out, I3, deco_2a4_1_d3);
  or or_1 (O, and_1_out, and_2_out, and_3_out, and_4_out);
endmodule

module \Comunicación_serie  (
  input  I0,
  input  I1,
  output S0,
  output S1
);

  wire Clk_out, multiplexer_1_out;

  Multiplexer #(.enable("false")) multiplexer_1 (.in0(I0), .in1(I1), .out(multiplexer_1_out), .sel(Clk_out));
  Clock Clk (.out(Clk_out));
  Demultiplexer #(.enable("false")) demultiplexer_1 (.out0(S0), .out1(S1), .in(multiplexer_1_out), .sel(Clk_out));
endmodule

module Alu_1 (
  input  Cin,
  input  A,
  input  [1:0] COp,
  input  B,
  output Y,
  output Cout
);

  wire adder_1_out, and_1_out, not_1_out, or_1_out;

  not not_1 (not_1_out, B);
  and and_1 (and_1_out, A, B);
  or or_1 (or_1_out, A, B);
  Adder #(.width(1)) adder_1 (.a(A), .b(B), .out(adder_1_out), .cin(Cin), .cout(Cout));
  Multiplexer #(.select(2)) multiplexer_1 (
    .in0(not_1_out), .in1(and_1_out), .in2(or_1_out), .in3(adder_1_out), .out(Y), .sel(COp));  // open: en
endmodule
