// Logisim project TP11.circ as structural Verilog: 4 circuits, main circuit Alu-1 8 Funciones
module Alu_1_8_Funciones (
  input  Cin,
  input  A,
  input  [1:0] COp,
  input  B,
  output O,
  output Cout
);

  wire adder_1_out, and_1_out, not_1_out, or_1_out;

  not not_1 (not_1_out, B);
  and and_1 (and_1_out, A, B);
  or or_1 (or_1_out, A, B);
  Adder #(.width(1)) adder_1 (.a(A), .b(B), .out(adder_1_out), .cin(Cin), .cout(Cout));
  Multiplexer #(.select(2)) multiplexer_1 (
    .in0(not_1_out), .in1(and_1_out), .in2(or_1_out), .in3(adder_1_out), .out(O), .sel(COp));  // open: en
endmodule

module Latch_D_AR (
  input  D,
  input  W_R_prime,
  input  AR,
  output Q
);

  wire nand_1_out, nand_2_out, nand_4_out, not_1_out;

  not not_1 (not_1_out, D);
  nand nand_1 (nand_1_out, D, W_R_prime);
  nand nand_2 (nand_2_out, W_R_prime, not_1_out);
  nand nand_3 (Q, nand_1_out, nand_4_out);
  nand nand_4 (nand_4_out, Q, nand_2_out, ~AR);  // NAND_Gate
endmodule

module Reg_1 (
  input  En,
  input  In,
  input  W_R_prime,
  input  AR,
  output O
);

  wire and_1_out, latch_d_ar_1_q, not_1_out;

  and and_1 (and_1_out, En, In);
  Latch_D_AR latch_d_ar_1 (.D(and_1_out), .W_R_prime(not_1_out), .Q(latch_d_ar_1_q), .AR(AR));
  not not_1 (not_1_out, W_R_prime);
  and and_2 (O, En, latch_d_ar_1_q, W_R_prime);

  // Notes on the sheet:
  //   In: pull=down
  //   and_2 drives only 1 and floats otherwise
endmodule

module RAM_32x8 (
  input  [4:0] Addr,
  input  [7:0] Data_Write,
  input  En,
  input  Clk,
  input  R_W_prime,
  input  AR,
  output [7:0] Data_Read
);

  RAM #(.addrWidth(5), .bus("separate")) ram_1 (
    .addr(Addr), .din(Data_Write), .data(Data_Read), .sel(En), .clk(Clk), .ld(R_W_prime), .clr(AR));  // open: str

  // Notes on the sheet:
  //   R_W_prime: pull=up
  //   AR: pull=up
  //   Clk: pull=up
endmodule
