// Logisim project TP7.circ as structural Verilog: 8 circuits, main circuit AND
module AND (
  input  A,
  input  B,
  output S___A_B
);

  and and_1 (S___A_B, A, B);
endmodule

module OR (
  input  A,
  input  B,
  output S___A___B
);

  or or_1 (S___A___B, A, B);

  // Notes on the sheet:
  //   S___A___B: pull=down
endmodule

module NOT (
  input  A,
  output S___A_prime
);

  not not_1 (S___A_prime, A);

  // Notes on the sheet:
  //   S___A_prime: pull=down
endmodule

module Asociativa_Producto (
  input  C,
  input  B,
  input  A,
  output S____AB_C,
  output S____AC_B,
  output S____BC_A,
  output S___ABC
);

  wire and_1_out, and_2_out, and_3_out;

  and and_1 (and_1_out, A, B);
  and and_2 (and_2_out, A, C);
  and and_3 (and_3_out, B, C);
  and and_4 (S___ABC, A, B, C);
  and and_5 (S____AB_C, and_1_out, C);
  and and_6 (S____AC_B, and_2_out, B);
  and and_7 (S____BC_A, and_3_out, A);
endmodule

module Asociativa_Suma (
  input  C,
  input  B,
  input  A,
  output S____AB_C,
  output S____AC_B,
  output S____BC_A,
  output S___ABC
);

  wire or_1_out, or_2_out, or_3_out;

  or or_1 (or_1_out, A, B);
  or or_2 (or_2_out, A, C);
  or or_3 (or_3_out, B, C);
  or or_4 (S___ABC, A, B, C);
  or or_5 (S____AB_C, or_1_out, C);
  or or_6 (S____AC_B, or_2_out, B);
  or or_7 (S____BC_A, or_3_out, A);
endmodule

module Distributiva_Producto_respecto_suma (
  input  C,
  input  B,
  input  A,
  output S___A__B_C,
  output S___A_B_A_C
);

  wire and_1_out, and_2_out, or_1_out;

  or or_1 (or_1_out, B, C);
  and and_1 (and_1_out, A, B);
  and and_2 (and_2_out, A, C);
  and and_3 (S___A__B_C, or_1_out, A);
  or or_2 (S___A_B_A_C, and_1_out, and_2_out);
endmodule

module AND_como_interruptor_de_datos (
  input  En,
  output Data_Out
);

  wire Data_In_out;

  Clock Data_In (.out(Data_In_out));
  and and_1 (Data_Out, Data_In_out, En);

  // Notes on the sheet:
  //   En: pull=up
endmodule

module OR_interruptor_de_datos (
  input  En,
  output Data_Out
);

  wire Data_In_out;

  Clock Data_In (.out(Data_In_out));
  or or_1 (Data_Out, Data_In_out, En);

  // Notes on the sheet:
  //   En: pull=up
endmodule
