// Logisim project TP8.circ as structural Verilog: 9 circuits, main circuit Ejercicio 1
module Ejercicio_1 (
  input  C,
  input  B,
  input  A,
  output out_4,
  output out_5
);

  wire and_1_out, or_1_out, or_2_out;

  and and_1 (and_1_out, B, C);
  or or_1 (or_1_out, A, B);
  or or_2 (or_2_out, A, C);
  or or_3 (out_4, A, and_1_out);
  and and_2 (out_5, or_1_out, or_2_out);

  // Notes on the sheet:
  //   A + (B.C) = (A + B).(A + C)
endmodule

module Ejercicio_2 (
  input  B,
  input  A,
  output out_3,
  output out_4
);

  wire and_1_out, not_1_out, not_2_out;

  not not_1 (not_1_out, A);
  not not_2 (not_2_out, B);
  not not_3 (out_3, and_1_out);
  and and_1 (and_1_out, A, B);
  or or_1 (out_4, not_1_out, not_2_out);

  // Notes on the sheet:
  //   (A.B)' = A' + B'
endmodule

module Ejercicio_3 (
  input  B,
  input  A,
  output out_3,
  output out_4
);

  wire not_1_out, not_2_out, or_1_out;

  not not_1 (not_1_out, A);
  not not_2 (not_2_out, B);
  not not_3 (out_3, or_1_out);
  or or_1 (or_1_out, A, B);
  and and_1 (out_4, not_1_out, not_2_out);

  // Notes on the sheet:
  //   (A + B)' = A' . B'
endmodule

module Ejercicio_4 (
  input  X,
  input  Y,
  output out_3,
  output out_4
);

  wire and_1_out, nand_1_out, not_1_out, not_2_out, or_1_out;

  not not_1 (not_1_out, X);
  not not_2 (not_2_out, Y);
  or or_1 (or_1_out, not_1_out, Y);
  and and_1 (and_1_out, not_2_out, X);
  not not_3 (out_3, or_1_out);
  not nand_1 (nand_1_out, and_1_out);  // NAND_Gate
  not not_4 (out_4, nand_1_out);

  // Notes on the sheet:
  //   (X' + Y)'
  //   [(X . Y')']'
endmodule

module Ejercicio_5 (
  input  C,
  input  B,
  input  A,
  output out_4,
  output out_5
);

  wire and_1_out, not_1_out, not_2_out, not_3_out;

  not not_1 (not_1_out, A);
  not not_2 (not_2_out, C);
  not not_3 (not_3_out, B);
  or or_1 (out_4, not_1_out, B, not_2_out);
  and and_1 (and_1_out, A, not_3_out, C);
  not nand_1 (out_5, and_1_out);  // NAND_Gate

  // Notes on the sheet:
  //   A' + B + C'
  //   (A . B' . C)'
endmodule

module Ejercicio_6 (
  input  X,
  input  Y,
  input  Z,
  output out_4,
  output out_5
);

  wire and_1_out, and_2_out, and_3_out, and_4_out, nand_1_out, nand_2_out, nand_3_out, not_1_out, not_2_out,
       not_3_out;

  not not_1 (not_1_out, Y);
  not not_2 (not_2_out, X);
  not not_3 (not_3_out, X);
  and and_1 (and_1_out, X, not_1_out, Z);
  and and_2 (and_2_out, not_2_out, Y);
  and and_3 (and_3_out, X, Y);
  nand nand_1 (nand_1_out, X, not_1_out, Z);
  nand nand_2 (nand_2_out, Y, not_3_out);
  nand nand_3 (nand_3_out, Y, X);
  and and_4 (and_4_out, nand_1_out, nand_2_out, nand_3_out);
  or or_1 (out_4, and_1_out, and_2_out, and_3_out);
  not nand_4 (out_5, and_4_out);  // NAND_Gate

  // Notes on the sheet:
  //   X.Y'.Z + X'.Y + X.Y
  //   ((X.Y'.Z)' . (X'.Y)' . (X.Y)')'
endmodule

module Ejercicio_7 (
  input  X,
  input  Y,
  input  Z,
  output out_4,
  output out_5
);

  wire and_1_out, and_2_out, and_3_out, nor_1_out, nor_2_out, nor_3_out, nor_4_out, not_1_out, not_2_out,
       not_3_out, not_4_out, not_5_out, not_6_out, not_7_out;

  not not_1 (not_1_out, Y);
  not not_2 (not_2_out, X);
  not not_3 (not_3_out, Y);
  not not_4 (not_4_out, Y);
  not not_5 (not_5_out, X);
  not not_6 (not_6_out, X);
  not not_7 (not_7_out, Z);
  and and_1 (and_1_out, X, not_1_out, Z);
  and and_2 (and_2_out, not_2_out, Y);
  and and_3 (and_3_out, X, Y);
  nor nor_1 (nor_1_out, not_6_out, Y, not_7_out);
  nor nor_2 (nor_2_out, not_3_out, X);
  nor nor_3 (nor_3_out, not_4_out, not_5_out);
  or or_1 (out_4, and_1_out, and_2_out, and_3_out);
  nor nor_4 (nor_4_out, nor_1_out, nor_2_out, nor_3_out);
  not not_8 (out_5, nor_4_out);

  // Notes on the sheet:
  //   X.Y'.Z + X'.Y + X.Y
  //   ((( X' + Y + Z')' + (X + Y')' + (X + Y')')')'
endmodule

module Ejercicio_8 (
  input  B,
  input  A,
  output out_3
);

  wire and_1_out, and_2_out, not_1_out, not_2_out;

  not not_1 (not_1_out, A);
  not not_2 (not_2_out, B);
  and and_1 (and_1_out, not_1_out, B);
  and and_2 (and_2_out, A, not_2_out);
  or or_1 (out_3, and_1_out, and_2_out);

  // Notes on the sheet:
  //   Y = A'B + AB'
endmodule

module Ejercicio_9 (
  input  B,
  input  A,
  output out_3
);

  wire and_1_out, and_2_out, not_1_out, not_2_out;

  not not_1 (not_1_out, A);
  not not_2 (not_2_out, B);
  and and_1 (and_1_out, A, B);
  and and_2 (and_2_out, not_1_out, not_2_out);
  or or_1 (out_3, and_1_out, and_2_out);

  // Notes on the sheet:
  //   Y = AB + A'B'
endmodule
