// Logisim project TP9.circ as structural Verilog: 13 circuits, main circuit Ejercicio 9
module Ejercicio_9 (
  input  C,
  input  B,
  input  A,
  output S
);

  wire and_1_out, and_2_out, not_1_out, not_2_out;

  not not_1 (not_1_out, C);
  not not_2 (not_2_out, not_1_out);
  and and_1 (and_1_out, A, ~B);  // AND_Gate
  and and_2 (and_2_out, ~A, B, C);  // AND_Gate
  or or_1 (S, and_1_out, and_2_out, not_2_out);

  // Notes on the sheet:
  //   S = A.B' + A'.B.C + C
endmodule

module Ejercicio_10 (
  input  X,
  input  Y,
  input  Z,
  output out_4
);

  wire and_1_out, and_2_out, not_1_out, not_2_out;

  not not_1 (not_1_out, X);
  not not_2 (not_2_out, Y);
  and and_1 (and_1_out, not_1_out, Y);
  and and_2 (and_2_out, X, not_2_out, Z);
  or or_1 (out_4, and_1_out, X, and_2_out);

  // Notes on the sheet:
  //    S = X + X'.Y + X.Y'.Z
endmodule

module Ejercicio_11 (
  input  C,
  input  B,
  input  A,
  output out_4
);

  wire and_1_out, and_2_out, and_3_out, and_4_out, and_5_out, not_1_out, not_2_out, not_3_out;

  not not_1 (not_1_out, C);
  not not_2 (not_2_out, B);
  not not_3 (not_3_out, A);
  and and_1 (and_1_out, not_3_out, not_2_out, not_1_out);
  and and_2 (and_2_out, not_3_out, not_2_out, C);
  and and_3 (and_3_out, not_3_out, B, C);
  and and_4 (and_4_out, not_3_out, B, not_1_out);
  and and_5 (and_5_out, A, not_2_out, C);
  or or_1 (out_4, and_1_out, and_2_out, and_3_out, and_4_out, and_5_out);

  // Notes on the sheet:
  //   S = A'B'C' + A'B'C + A'BC + A'BC' + AB'C
endmodule

module Ejercicio_12 (
  input  C,
  input  B,
  input  A,
  output out_4
);

  wire and_1_out, and_2_out, and_3_out, and_4_out, not_1_out, not_2_out, not_3_out;

  not not_1 (not_1_out, C);
  not not_2 (not_2_out, B);
  not not_3 (not_3_out, A);
  and and_1 (and_1_out, not_3_out, not_2_out, C);
  and and_2 (and_2_out, not_3_out, B, not_1_out);
  and and_3 (and_3_out, A, not_2_out, not_1_out);
  and and_4 (and_4_out, A, B, C);
  or or_1 (out_4, and_1_out, and_2_out, and_3_out, and_4_out);

  // Notes on the sheet:
  //   S = A'B'C + A'BC'  + AB'C'  + ABC
endmodule

module Ejercicio_13 (
  input  C,
  input  B,
  input  A,
  output out_4
);

  wire and_1_out, and_2_out, and_3_out, and_4_out, not_1_out, not_2_out, not_3_out;

  not not_1 (not_1_out, C);
  not not_2 (not_2_out, B);
  not not_3 (not_3_out, A);
  and and_1 (and_1_out, not_3_out, not_2_out, not_1_out);
  and and_2 (and_2_out, not_3_out, not_2_out, C);
  and and_3 (and_3_out, not_3_out, B, C);
  and and_4 (and_4_out, A, B, not_1_out);
  or or_1 (out_4, and_1_out, and_2_out, and_3_out, and_4_out);

  // Notes on the sheet:
  //   S = A'B'C' + A'B'C  + A'BC  + ABC' 
endmodule

module Ejercicio_14 (
  input  C,
  input  B,
  input  A,
  output out_4
);

  wire not_1_out, not_2_out, not_3_out, or_1_out, or_2_out, or_3_out, or_4_out;

  not not_1 (not_1_out, C);
  not not_2 (not_2_out, B);
  not not_3 (not_3_out, A);
  or or_1 (or_1_out, A, not_2_out, C);
  or or_2 (or_2_out, not_3_out, B, C);
  or or_3 (or_3_out, not_3_out, B, not_1_out);
  or or_4 (or_4_out, not_3_out, not_2_out, not_1_out);
  and and_1 (out_4, or_1_out, or_2_out, or_3_out, or_4_out);

  // Notes on the sheet:
  //   S = (A+B'+C)(A'+B+C)(A'+B+C')(A'+B'+C')
endmodule

module Ejercicio_15 (
  input  C,
  input  B,
  input  A,
  output out_4
);

  wire and_1_out, and_2_out, and_3_out, and_4_out, not_1_out, not_2_out, not_3_out;

  not not_1 (not_1_out, C);
  not not_2 (not_2_out, B);
  not not_3 (not_3_out, A);
  and and_1 (and_1_out, A, not_2_out, not_1_out);
  and and_2 (and_2_out, not_3_out, B, not_1_out);
  and and_3 (and_3_out, not_3_out, not_2_out, C);
  and and_4 (and_4_out, A, B, C);
  or or_1 (out_4, and_1_out, and_2_out, and_3_out, and_4_out);

  // Notes on the sheet:
  //    O = AB'C' + A'BC' + A'B'C  + ABC
endmodule

module Ejercicio_16 (
  input  C,
  input  B,
  input  A,
  output out_4
);

  wire not_1_out;

  not not_1 (not_1_out, C);
  or or_1 (out_4, B, not_1_out);

  // Notes on the sheet:
  //   S = B + C'
endmodule

module Ejercicio_17 (
  input  A,
  input  B,
  input  C,
  input  D,
  input  A_2,
  input  B_2,
  input  C_2,
  input  D_2,
  output out_9,
  output out_10
);

  wire and_1_out, and_2_out, and_3_out, and_4_out, not_1_out, not_2_out;

  not not_1 (not_1_out, A);
  not not_2 (not_2_out, C);
  and and_1 (and_1_out, not_1_out, B, not_2_out, D);
  and and_2 (and_2_out, not_1_out, B, C, D);
  and and_3 (and_3_out, A, B, not_2_out, D);
  and and_4 (and_4_out, A, B, C, D);
  and and_5 (out_10, D_2, B_2);
  or or_1 (out_9, and_1_out, and_2_out, and_3_out, and_4_out);

  // Notes on the sheet:
  //   S = A'BC'D + A'BCD + ABC'D + ABCD 
  //   S = BD
endmodule

module Ejercicio_18 (
  input  A,
  input  B,
  input  C,
  input  D,
  output out_5
);

  wire not_1_out;

  not not_1 (not_1_out, C);
  or or_1 (out_5, not_1_out, B);

  // Notes on the sheet:
  //   S = B + C'
endmodule

module Sum_1 (
  input  A,
  input  B,
  input  Cin,
  output Salida,
  output Carry_Out
);

  wire and_1_out, and_2_out, xor_1_out;

  xor xor_1 (xor_1_out, A, B);
  and and_1 (and_1_out, A, B);
  xor xor_2 (Salida, xor_1_out, Cin);
  and and_2 (and_2_out, xor_1_out, Cin);
  xor xor_3 (Carry_Out, and_2_out, and_1_out);
endmodule

module Sum_4 (
  input  [3:0] A0_3,
  input  [3:0] B0_3,
  output [3:0] O0_3,
  output Co
);

  wire sum_1_1_carry_out, sum_1_2_carry_out, sum_1_3_carry_out;

  Sum_1 sum_1_1 (.A(A0_3[0]), .B(B0_3[0]), .Cin(1'b0), .Salida(O0_3[0]), .Carry_Out(sum_1_1_carry_out));
  Sum_1 sum_1_2 (.A(A0_3[1]), .B(B0_3[1]), .Cin(sum_1_1_carry_out), .Salida(O0_3[1]), .Carry_Out(sum_1_2_carry_out));
  Sum_1 sum_1_3 (.A(A0_3[2]), .B(B0_3[2]), .Cin(sum_1_2_carry_out), .Salida(O0_3[2]), .Carry_Out(sum_1_3_carry_out));
  Sum_1 sum_1_4 (.A(A0_3[3]), .B(B0_3[3]), .Cin(sum_1_3_carry_out), .Salida(O0_3[3]), .Carry_Out(Co));
endmodule

module Sum_8_Nativo (
  input  [7:0] A0_7,
  input  [7:0] A0_7_2,
  output [7:0] O0_7,
  output out_4
);

  Adder adder_1 (.a(A0_7), .b(A0_7_2), .out(O0_7), .cin(1'b0), .cout(out_4));
endmodule
